// Logisim project final_单周期cpu.circ as structural Verilog: 11 circuits, main circuit main
module main (
  input  reset,
  output [31:0] out_2,
  output out_3,
  output [4:0] out_4,
  output [31:0] out_5,
  output out_6,
  output [4:0] out_7,
  output [31:0] out_8
);

  wire and_1_out, branch, clk, is0, memToReg, regDst, src1, src2;
  wire [1:0] EXTop;
  wire [2:0] ALUctr;
  wire [4:0] \取2_6位_1_out_2 ;
  wire [31:0] adder_1_out, adder_2_out, aluOut, DMout, imm32, multiplexer_2_out, multiplexer_3_out,
       multiplexer_4_out, PC_q, read1, shifter_1_out;

  Clock clock_1 (.out(clk));
  \取2_6位  \u_取2_6位_1  (.in_1(PC_q), .out_2(\取2_6位_1_out_2 ));
  Register #(.width(32)) PC (.D(multiplexer_2_out), .Q(PC_q), .clk(clk), .clr(reset));  // open: en
  Adder #(.width(32)) adder_1 (.a(PC_q), .b(32'h4), .out(adder_1_out));  // open: cin, cout
  realcontrol realcontrol_1 (
    ._31_26(out_2[31:26]), ._5_0(out_2[5:0]), .regDest(regDst), .ALUSource(src1), .ALUSrc2(src2),
    .MemToReg(memToReg), .regwrite(out_3), .memWrite(out_6), .branch(branch), .extOp(EXTop), .ALUCtr(ALUctr));
  Multiplexer #(.width(5), .enable("false")) multiplexer_1 (
    .in0(out_2[20:16]), .in1(out_2[15:11]), .out(out_4), .sel(regDst));
  Shifter #(.width(32)) shifter_1 (.in(imm32), .\dist (5'b00010), .out(shifter_1_out));
  ROM #(.addrWidth(5), .dataWidth(32)) rom_1 (.addr(\取2_6位_1_out_2 ), .data(out_2));  // open: sel
  Adder #(.width(32)) adder_2 (.a(adder_1_out), .b(shifter_1_out), .out(adder_2_out));  // open: cin, cout
  Multiplexer #(.width(32)) multiplexer_2 (
    .in0(adder_1_out), .in1(adder_2_out), .out(multiplexer_2_out), .sel(and_1_out));  // open: en
  and and_1 (and_1_out, branch, is0);
  grfs grfs_1 (
    .a1(out_2[25:21]), .a2(out_2[20:16]), .a3(out_4), .wd(out_5), .in_1(clk), .in_2(reset), .in_3(out_3),
    .rd1(read1), .rd2(out_8));
  EXT EXT (.pre(out_2[15:0]), .op(EXTop), .out_3(imm32));
  Multiplexer #(.width(32), .enable("false")) multiplexer_3 (
    .in0(read1), .in1({32{1'b0}}), .out(multiplexer_3_out), .sel(src2));
  Multiplexer #(.width(32), .enable("false")) multiplexer_4 (
    .in0(out_8), .in1(imm32), .out(multiplexer_4_out), .sel(src1));
  ALU ALU (.input1(multiplexer_3_out), .input2(multiplexer_4_out), .op(ALUctr), .iszero(is0), .out_5(aluOut));
  \取2_6位  \u_取2_6位_2  (.in_1(aluOut), .out_2(out_7));
  Multiplexer #(.width(32), .enable("false")) multiplexer_5 (.in0(aluOut), .in1(DMout), .out(out_5), .sel(memToReg));
  RAM #(.addrWidth(5), .dataWidth(32), .bus("separate")) ram_1 (
    .addr(out_7), .din(out_8), .data(DMout), .str(out_6), .clk(clk), .clr(reset));  // open: sel, ld

  // Other names for the same wires on the sheet: _0 = out_2[0]; _5_0[5:0] = out_2[5:0]; _15_0imm[15:0] = out_2[15:0];
  //   _25_0[25:0] = out_2[25:0]; ins[31:0] = out_2; _1 = out_2[1]; _2 = out_2[2]; _3 = out_2[3]; _4 = out_2[4];
  //   _5 = out_2[5]; _11 = out_2[11]; _15_11rd[4:0] = out_2[15:11]; _12 = out_2[12]; _13 = out_2[13]; _14 = out_2[14];
  //   _15 = out_2[15]; _16 = out_2[16]; _20_16rt[4:0] = out_2[20:16]; _17 = out_2[17]; _18 = out_2[18];
  //   _19 = out_2[19]; _20 = out_2[20]; _21 = out_2[21]; _25_21rs[4:0] = out_2[25:21]; _22 = out_2[22];
  //   _23 = out_2[23]; _24 = out_2[24]; _25 = out_2[25]; _26 = out_2[26]; _31_26[5:0] = out_2[31:26]; _27 = out_2[27];
  //   _28 = out_2[28]; _29 = out_2[29]; _30 = out_2[30]; _31 = out_2[31]; _6 = out_2[6]; _7 = out_2[7]; _8 = out_2[8];
  //   _9 = out_2[9]; _10 = out_2[10]; MemAddr[4:0] = out_7; MemWriteAns = out_6; re = reset; read2[31:0] = out_8;
  //   regAdr[4:0] = out_4; regWriteAns = out_3; writeRegData[31:0] = out_5

  // Notes on the sheet:
  //   WriteWhatReg
  //   contents of rom_1 (hex, n*v repeats v):
  //   3404007b 348501c8 3c06007b 3c07ffff 34e7ffff 868020 878820 e79020 34080000 ad040000 ad050004
  //   ad060008 ad07000c ad100010 ad110014 ad120018 8d040000 8d05000c ad04001c ad050020 34040001 34050002
  //   34060001 10850001 10860001 ad040024 ad050028
  //   GRF
  //   EXT扩展
  //   ALU
  //   DM
  //   WhatToWriteBack
endmodule

module \取2_6位  (
  input  [31:0] in_1,
  output [4:0] out_2
);


  assign out_2 = in_1[6:2];
endmodule

module EXT (
  input  [15:0] pre,
  input  [1:0] op,
  output [31:0] out_3
);

  wire [31:0] bit_extender_1_out, bit_extender_2_out;

  assign bit_extender_1_out = {{16{1'b0}}, pre};  // Bit_Extender bit_extender_1
  assign bit_extender_2_out = {{16{1'b1}}, pre};  // Bit_Extender bit_extender_2
  Multiplexer #(.select(2), .width(32)) multiplexer_1 (
    .in0(bit_extender_1_out), .in1(bit_extender_2_out), .in2({pre, {16{1'b0}}}), .out(out_3), .sel(op));  // open: in3, en
endmodule

module ALU (
  input  [2:0] op,
  input  [31:0] input1,
  input  [31:0] input2,
  output iszero,
  output [31:0] out_5
);

  wire [31:0] adder_1_out, or_1_out, subtractor_1_out;

  Adder #(.width(32)) adder_1 (.a(input1), .b(input2), .out(adder_1_out));  // open: cin, cout
  Subtractor #(.width(32)) subtractor_1 (.a(input1), .b(input2), .out(subtractor_1_out));  // open: bin, bout
  assign or_1_out = input1 | input2;  // OR_Gate or_1, 32 bits wide
  Multiplexer #(.select(3), .width(32)) multiplexer_1 (
    .in0(adder_1_out), .in1(subtractor_1_out), .in2(or_1_out), .out(out_5), .sel(op));  // open: in3, in4, in5, in6, in7, en
  Comparator #(.width(32)) comparator_1 (.a({32{1'b0}}), .b(out_5), .eq(iszero));  // open: gt, lt
endmodule

module regs (
  input  [4:0] in_1,
  input  c,
  input  r,
  input  [31:0] in0,
  input  [31:0] in1,
  input  [31:0] in2,
  input  [31:0] in3,
  input  [31:0] in_t4,
  input  [31:0] in_9,
  input  [31:0] in_10,
  input  [31:0] in_11,
  input  [31:0] in8,
  input  [31:0] in_13,
  input  [31:0] in_14,
  input  [31:0] in_15,
  input  [31:0] in_16,
  input  [31:0] in_17,
  input  [31:0] in_18,
  input  [31:0] in_19,
  input  [31:0] in_20,
  input  [31:0] in_21,
  input  [31:0] in_22,
  input  [31:0] in_23,
  input  [31:0] in_24,
  input  [31:0] in_25,
  input  [31:0] in_26,
  input  [31:0] in_27,
  input  [31:0] in_28,
  input  [31:0] in_29,
  input  [31:0] in_30,
  input  [31:0] in_31,
  input  [31:0] in_32,
  input  [31:0] in_33,
  input  [31:0] in_34,
  input  [31:0] in_35,
  output [31:0] out0,
  output [31:0] out1,
  output [31:0] out2,
  output [31:0] out3,
  output [31:0] out_40,
  output [31:0] out_41,
  output [31:0] out_42,
  output [31:0] out_43,
  output [31:0] out_44,
  output [31:0] out_45,
  output [31:0] out_46,
  output [31:0] out_47,
  output [31:0] out_48,
  output [31:0] out_49,
  output [31:0] out_50,
  output [31:0] out_51,
  output [31:0] out_52,
  output [31:0] out_53,
  output [31:0] out_54,
  output [31:0] out_55,
  output [31:0] out_56,
  output [31:0] out_57,
  output [31:0] out_58,
  output [31:0] out_59,
  output [31:0] out_60,
  output [31:0] out_61,
  output [31:0] out_62,
  output [31:0] out_63,
  output [31:0] out_64,
  output [31:0] out_65,
  output [31:0] out_66,
  output [31:0] out_67
);

  wire en0, en1, en2, en3, en4, en5, en6, en7, en8, en9, en10, en11, en12, en13, en14, en15, en16, en17,
       en18, en19, en20, en21, en22, en23, en24, en25, en26, en27, en28, en29, en30, en31;

  Register #(.width(32)) _0 (.D(in0), .Q(out0), .clk(c), .clr(1'b1));  // open: en
  Register #(.width(32)) _1 (.D(in_t4), .en(en4), .Q(out_40), .clk(c), .clr(r));
  Register #(.width(32)) _2 (.D(in8), .en(en8), .Q(out_44), .clk(c), .clr(r));
  Register #(.width(32)) _3 (.D(in_16), .en(en12), .Q(out_48), .clk(c), .clr(r));
  Register #(.width(32)) _4 (.D(in_20), .en(en16), .Q(out_52), .clk(c), .clr(r));
  Register #(.width(32)) _5 (.D(in_24), .en(en20), .Q(out_56), .clk(c), .clr(r));
  Register #(.width(32)) _6 (.D(in_28), .en(en24), .Q(out_60), .clk(c), .clr(r));
  Register #(.width(32)) _7 (.D(in_32), .en(en28), .Q(out_64), .clk(c), .clr(r));
  Register #(.width(32)) _8 (.D(in1), .en(en1), .Q(out1), .clk(c), .clr(r));
  Register #(.width(32)) _9 (.D(in_9), .en(en5), .Q(out_41), .clk(c), .clr(r));
  Register #(.width(32)) _10 (.D(in_13), .en(en9), .Q(out_45), .clk(c), .clr(r));
  Register #(.width(32)) _11 (.D(in_17), .en(en13), .Q(out_49), .clk(c), .clr(r));
  Register #(.width(32)) _12 (.D(in_21), .en(en17), .Q(out_53), .clk(c), .clr(r));
  Register #(.width(32)) _13 (.D(in_25), .en(en21), .Q(out_57), .clk(c), .clr(r));
  Register #(.width(32)) _14 (.D(in_29), .en(en25), .Q(out_61), .clk(c), .clr(r));
  Register #(.width(32)) _15 (.D(in_33), .en(en29), .Q(out_65), .clk(c), .clr(r));
  Register #(.width(32)) _16 (.D(in2), .en(en2), .Q(out2), .clk(c), .clr(r));
  Register #(.width(32)) _17 (.D(in_10), .en(en6), .Q(out_42), .clk(c), .clr(r));
  Register #(.width(32)) _18 (.D(in_14), .en(en10), .Q(out_46), .clk(c), .clr(r));
  Register #(.width(32)) _19 (.D(in_18), .en(en14), .Q(out_50), .clk(c), .clr(r));
  Register #(.width(32)) _20 (.D(in_22), .en(en18), .Q(out_54), .clk(c), .clr(r));
  Register #(.width(32)) _21 (.D(in_26), .en(en22), .Q(out_58), .clk(c), .clr(r));
  Register #(.width(32)) _22 (.D(in_30), .en(en26), .Q(out_62), .clk(c), .clr(r));
  Register #(.width(32)) _23 (.D(in_34), .en(en30), .Q(out_66), .clk(c), .clr(r));
  Register #(.width(32)) _24 (.D(in3), .en(en3), .Q(out3), .clk(c), .clr(r));
  Register #(.width(32)) _25 (.D(in_11), .en(en7), .Q(out_43), .clk(c), .clr(r));
  Register #(.width(32)) _26 (.D(in_15), .en(en11), .Q(out_47), .clk(c), .clr(r));
  Register #(.width(32)) _27 (.D(in_19), .en(en15), .Q(out_51), .clk(c), .clr(r));
  Register #(.width(32)) _28 (.D(in_23), .en(en19), .Q(out_55), .clk(c), .clr(r));
  Register #(.width(32)) _29 (.D(in_27), .en(en23), .Q(out_59), .clk(c), .clr(r));
  Register #(.width(32)) _30 (.D(in_31), .en(en27), .Q(out_63), .clk(c), .clr(r));
  Register #(.width(32)) _31 (.D(in_35), .en(en31), .Q(out_67), .clk(c), .clr(r));
  Decoder #(.select(5)) decoder_1 (
    .out0(en0), .out1(en1), .out2(en2), .out3(en3), .out4(en4), .out5(en5), .out6(en6), .out7(en7),
    .out8(en8), .out9(en9), .out10(en10), .out11(en11), .out12(en12), .out13(en13), .out14(en14),
    .out15(en15), .out16(en16), .out17(en17), .out18(en18), .out19(en19), .out20(en20), .out21(en21),
    .out22(en22), .out23(en23), .out24(en24), .out25(en25), .out26(en26), .out27(en27), .out28(en28),
    .out29(en29), .out30(en30), .out31(en31), .sel(in_1));  // open: en

  // Other names for the same wires on the sheet: cp = c; w[4:0] = in_1
endmodule

module grfs (
  input  in_1,
  input  in_2,
  input  in_3,
  input  [4:0] a1,
  input  [4:0] a2,
  input  [4:0] a3,
  input  [31:0] wd,
  output [31:0] rd1,
  output [31:0] rd2
);

  wire [4:0] multiplexer_1_out;
  wire [31:0] _0, _1, _2, _3, _4, _5, _6, _7, _8, _9, _10, _11, _12, _13, _14, _15, _16, _17, _18, _19, _20,
       _21, _22, _23, _24, _25, _26, _27, _28, _29, _30, _31;

  Multiplexer #(.width(5), .enable("false")) multiplexer_1 (
    .in0({5{1'b0}}), .in1(a3), .out(multiplexer_1_out), .sel(in_3));
  regs regs_1 (
    .in_1(multiplexer_1_out), .c(in_1), .r(in_2), .in0(wd), .in1(wd), .in2(wd), .in3(wd), .in_t4(wd),
    .in_9(wd), .in_10(wd), .in_11(wd), .in8(wd), .in_13(wd), .in_14(wd), .in_15(wd), .in_16(wd), .in_17(wd),
    .in_18(wd), .in_19(wd), .in_20(wd), .in_21(wd), .in_22(wd), .in_23(wd), .in_24(wd), .in_25(wd),
    .in_26(wd), .in_27(wd), .in_28(wd), .in_29(wd), .in_30(wd), .in_31(wd), .in_32(wd), .in_33(wd),
    .in_34(wd), .in_35(wd), .out0(_0), .out1(_1), .out2(_2), .out3(_3), .out_40(_4), .out_41(_5),
    .out_42(_6), .out_43(_7), .out_44(_8), .out_45(_9), .out_46(_10), .out_47(_11), .out_48(_12),
    .out_49(_13), .out_50(_14), .out_51(_15), .out_52(_16), .out_53(_17), .out_54(_18), .out_55(_19),
    .out_56(_20), .out_57(_21), .out_58(_22), .out_59(_23), .out_60(_24), .out_61(_25), .out_62(_26),
    .out_63(_27), .out_64(_28), .out_65(_29), .out_66(_30), .out_67(_31));
  Multiplexer #(.select(5), .width(32)) multiplexer_2 (
    .in0(_0), .in1(_1), .in2(_2), .in3(_3), .in4(_4), .in5(_5), .in6(_6), .in7(_7), .in8(_8), .in9(_9),
    .in10(_10), .in11(_11), .in12(_12), .in13(_13), .in14(_14), .in15(_15), .in16(_16), .in17(_17),
    .in18(_18), .in19(_19), .in20(_20), .in21(_21), .in22(_22), .in23(_23), .in24(_24), .in25(_25),
    .in26(_26), .in27(_27), .in28(_28), .in29(_29), .in30(_30), .in31(_31), .out(rd1), .sel(a1));  // open: en
  Multiplexer #(.select(5), .width(32)) multiplexer_3 (
    .in0(_0), .in1(_1), .in2(_2), .in3(_3), .in4(_4), .in5(_5), .in6(_6), .in7(_7), .in8(_8), .in9(_9),
    .in10(_10), .in11(_11), .in12(_12), .in13(_13), .in14(_14), .in15(_15), .in16(_16), .in17(_17),
    .in18(_18), .in19(_19), .in20(_20), .in21(_21), .in22(_22), .in23(_23), .in24(_24), .in25(_25),
    .in26(_26), .in27(_27), .in28(_28), .in29(_29), .in30(_30), .in31(_31), .out(rd2), .sel(a2));  // open: en

  // Other names for the same wires on the sheet: clk = in_1; reset = in_2; we = in_3
endmodule

module realcontrol (
  input  [5:0] _31_26,
  input  [5:0] _5_0,
  output regDest,
  output ALUSource,
  output ALUSrc2,
  output MemToReg,
  output regwrite,
  output memWrite,
  output branch,
  output [1:0] extOp,
  output [2:0] ALUCtr
);

  wire add, and_2_out, and_3_out, and_4_out, beq, lw, nop, not_1_out, not_2_out, not_3_out, not_4_out,
       not_5_out, not_6_out, not_7_out, not_8_out, not_9_out, not_10_out, not_11_out, not_12_out, not_13_out,
       not_14_out, not_15_out, not_16_out, not_17_out, not_18_out, not_19_out, not_20_out, not_21_out,
       not_22_out, not_23_out, not_24_out, op0, ori, sub, sw;

  not not_1 (not_1_out, _31_26[5]);
  not not_2 (not_2_out, _31_26[4]);
  not not_3 (not_3_out, _31_26[3]);
  not not_4 (not_4_out, _31_26[2]);
  not not_5 (not_5_out, _31_26[1]);
  not not_6 (not_6_out, _31_26[0]);
  not not_7 (not_7_out, _5_0[5]);
  not not_8 (not_8_out, _5_0[4]);
  not not_9 (not_9_out, _5_0[3]);
  not not_10 (not_10_out, _5_0[2]);
  not not_11 (not_11_out, _5_0[1]);
  not not_12 (not_12_out, _5_0[0]);
  not not_13 (not_13_out, _31_26[5]);
  not not_14 (not_14_out, _31_26[4]);
  not not_15 (not_15_out, _31_26[3]);
  not not_16 (not_16_out, _31_26[2]);
  not not_17 (not_17_out, _31_26[1]);
  not not_18 (not_18_out, _31_26[0]);
  not not_19 (not_19_out, _5_0[5]);
  not not_20 (not_20_out, _5_0[4]);
  not not_21 (not_21_out, _5_0[3]);
  not not_22 (not_22_out, _5_0[2]);
  not not_23 (not_23_out, _5_0[1]);
  not not_24 (not_24_out, _5_0[0]);
  and and_1 (ALUSrc2, not_1_out, not_2_out, _31_26[3], _31_26[2], _31_26[1], _31_26[0]);
  and and_2 (and_2_out, _5_0[5], not_8_out, not_9_out, not_10_out, not_11_out, not_12_out);
  and and_3 (and_3_out, _5_0[5], not_8_out, not_9_out, not_10_out, _5_0[1], not_12_out);
  and and_4 (and_4_out, not_7_out, not_8_out, not_9_out, not_10_out, not_11_out, not_12_out);
  and and_5 (ori, not_1_out, not_2_out, _31_26[3], _31_26[2], not_5_out, _31_26[0]);
  and and_6 (lw, _31_26[5], not_2_out, not_3_out, not_4_out, _31_26[1], _31_26[0]);
  and and_7 (sw, _31_26[5], not_2_out, _31_26[3], not_4_out, _31_26[1], _31_26[0]);
  and and_8 (op0, not_1_out, not_2_out, not_3_out, not_4_out, not_5_out, not_6_out);
  and and_9 (beq, not_1_out, not_2_out, not_3_out, _31_26[2], not_5_out, not_6_out);
  and and_10 (add, op0, and_2_out);
  and and_11 (sub, op0, and_3_out);
  and and_12 (nop, op0, and_4_out);
  or or_1 (regDest, add, sub);
  or or_2 (ALUSource, ori, lw, sw, ALUSrc2);
  buf or_3 (MemToReg, lw);  // OR_Gate
  or or_4 (regwrite, add, sub, ori, lw, ALUSrc2);
  buf or_5 (memWrite, sw);  // OR_Gate
  buf or_6 (branch, beq);  // OR_Gate
  buf or_7 (extOp[1], ALUSrc2);  // OR_Gate
  or or_8 (extOp[0], beq, lw, sw);
  buf or_9 (ALUCtr[1], ori);  // OR_Gate
  or or_10 (ALUCtr[0], sub, beq);

  assign ALUCtr[2] = 1'b0;

  // Other names for the same wires on the sheet: func[5:0] = _5_0; lui = ALUSrc2; op[5:0] = _31_26

  // Notes on the sheet:
  //   以下为了方便改：
  //   op为000000
  //   =1写入
  //   =1写入
  //   000加001减010or
  //   =0（写入寄存器为rt）=1（写入寄存器为rd）
  //   =1的时候说明是beq指令
  //   =0（选read2）=1（选扩展后的立即数）
  //   =0（选read1）=1（选0）
  //   =0（选ALU）=1（选DM）
  //   00零扩展，01符号扩展，10加载至高位
endmodule

module \分32位  (
  input  [31:0] in_1,
  output [31:0] out_2
);


  assign out_2 = in_1;

  // Other names for the same wires on the sheet: _0 = in_1[0]; _1 = in_1[1]; _2 = in_1[2]; _3 = in_1[3]; _4 = in_1[4];
  //   _5 = in_1[5]; _6 = in_1[6]; _7 = in_1[7]; _8 = in_1[8]; _9 = in_1[9]; _10 = in_1[10]; _11 = in_1[11];
  //   _12 = in_1[12]; _13 = in_1[13]; _14 = in_1[14]; _15 = in_1[15]; _16 = in_1[16]; _17 = in_1[17]; _18 = in_1[18];
  //   _19 = in_1[19]; _20 = in_1[20]; _21 = in_1[21]; _22 = in_1[22]; _23 = in_1[23]; _24 = in_1[24]; _25 = in_1[25];
  //   _26 = in_1[26]; _27 = in_1[27]; _28 = in_1[28]; _29 = in_1[29]; _30 = in_1[30]; _31 = in_1[31]

  // Notes on the sheet:
  //   分32位
  //   合32位
endmodule

module \分32位2  (
  input  [31:0] in_1
);

  // NOT_Gate not_1 has open pins: in=in_1[0], out=open
  // NOT_Gate not_2 has open pins: in=in_1[1], out=open
  // NOT_Gate not_3 has open pins: in=in_1[2], out=open
  // NOT_Gate not_4 has open pins: in=in_1[3], out=open
  // NOT_Gate not_5 has open pins: in=in_1[4], out=open
  // NOT_Gate not_6 has open pins: in=in_1[5], out=open
  // NOT_Gate not_7 has open pins: in=in_1[6], out=open
  // NOT_Gate not_8 has open pins: in=in_1[7], out=open
endmodule

module \为了详细地看一看control  (
  input  in_1,
  input  in_2,
  input  in_3,
  input  in_4,
  input  in_5,
  input  in_6,
  input  in_7,
  output regDest,
  output ALUSource,
  output ALUSrc2,
  output MemToReg,
  output regwrite,
  output memWrite,
  output branch,
  output [1:0] extOp,
  output [2:0] ALUCtr
);

  or or_1 (regDest, in_1, in_2);
  or or_2 (ALUSource, in_3, in_4, in_5, in_7);
  buf or_3 (MemToReg, in_4);  // OR_Gate
  or or_4 (regwrite, in_1, in_2, in_3, in_4, in_7);
  buf or_5 (memWrite, in_5);  // OR_Gate
  buf or_6 (branch, in_6);  // OR_Gate
  buf or_7 (extOp[1], in_7);  // OR_Gate
  or or_8 (extOp[0], in_6, in_4, in_5);
  buf or_9 (ALUCtr[1], in_3);  // OR_Gate
  or or_10 (ALUCtr[0], in_2, in_6);

  assign ALUCtr[2] = 1'b0;
  assign ALUSrc2 = in_7;

  // Other names for the same wires on the sheet: add = in_1; beq = in_6; lui = in_7; lw = in_4; ori = in_3;
  //   sub = in_2; sw = in_5
endmodule

module \认识logisim  (
  input  in_1,
  input  \有三态 ,
  input  [7:0] in_3,
  input  [7:0] in_4,
  input  in_5,
  input  in_6,
  input  in_7,
  input  in_8,
  input  in_9,
  input  in_10,
  input  in_11,
  input  in_12,
  input  in_13,
  input  in_14,
  input  in_15,
  input  in_16,
  input  in_17,
  input  \加载 ,
  input  \移位 ,
  input  in_20,
  input  in_21,
  input  in_22,
  input  in_23,
  input  in_24,
  input  reset,
  input  [7:0] in_26,
  input  [7:0] in_27,
  input  [2:0] in_28,
  input  [1:0] in_29,
  input  [1:0] in_30,
  input  [1:0] in_31,
  input  [1:0] in_32,
  input  [7:0] in_33,
  input  [2:0] in_34,
  input  [1:0] in_35,
  input  [1:0] in_36,
  input  [1:0] in_37,
  input  [1:0] in_38,
  input  [7:0] in_39,
  input  in_40,
  input  in_41,
  input  [7:0] in_42,
  output [7:0] out_43,
  output out_44,
  output out_45,
  output out_46,
  output out_47,
  output out_48,
  output [1:0] \得到最高为1的位置 ,
  output out_50,
  output out_51,
  output out_52,
  output out_53,
  output out_54,
  output out_55,
  output out_56,
  output out_57,
  output out_58,
  output out_59,
  output out_60,
  output [7:0] out_61,
  output [1:0] out_62,
  output [7:0] out_63,
  output [1:0] out_64,
  output [3:0] out_65,
  output out_66,
  output [2:0] out_67,
  output [2:0] \找最高的1 ,
  output [2:0] out_69
);

  wire clock_1_out, clock_2_out, subtractor_1_bout, transmission_1_p1, undriven_6;
  wire [7:0] divider_1_out, divider_1_rem, multiplier_1_cout, multiplier_1_out, subtractor_1_out, undriven,
       undriven_2, undriven_3, undriven_4, undriven_5, undriven_7, undriven_8, undriven_9;

  Pull_Resistor pull_resistor_1 ();  // open: node
  // Probe on nothing
  Clock clock_1 (.out(clock_1_out));
  Transistor transistor_1 ();  // open: in, out, gate
  // Transmission_Gate transmission_1: pin names not known; wires that end beside it: transmission_1_p1, 1'b0, clock_1_out, 1'b1
  Bit_Extender bit_extender_1 ();  // open: in, out
  // Buffer buffer_1 is placed but not wired
  assign out_66 = in_41 ? in_40 : 1'bz;  // Controlled_Buffer controlled_buffer_1
  Controlled_Inverter controlled_inverter_1 ();  // open: in, out, en
  // NOT_Gate not_1 is placed but not wired
  // AND_Gate and_1 is placed but not wired
  // OR_Gate or_1 is placed but not wired
  // NAND_Gate nand_1 is placed but not wired
  // NOR_Gate nor_1 is placed but not wired
  // NOR_Gate nor_2 is placed but not wired
  // XNOR_Gate xnor_1 is placed but not wired
  assign out_62 = in_29 ^ in_30 ^ in_31 ^ in_32;  // Odd_Parity odd_parity_1, 2 bits wide
  assign out_64 = ~(in_35 ^ in_36 ^ in_37 ^ in_38);  // Even_Parity even_parity_1, 2 bits wide
  Multiplexer multiplexer_1 ();  // open: in0, in1, out, sel, en
  Demultiplexer #(.enable("false")) demultiplexer_1 (.out0(out_44), .out1(out_46), .in(in_6), .sel(in_16));
  Decoder #(.enable("false")) decoder_1 (.out0(out_47), .out1(out_48), .sel(in_17));
  Priority_Encoder #(.select(2)) priority_encoder_1 (
    .in0(in_20), .in1(in_21), .in2(in_23), .in3(in_24), .out(\得到最高为1的位置 ), .gs(out_51));  // open: en_out, en_in
  BitSelector bitselector_1 (.in(in_26), .out(out_52), .sel(in_28));
  Adder adder_1 (.a(in_3), .b(in_4), .out(out_43), .cin(in_1), .cout(out_45));
  Subtractor subtractor_1 (
    .a(undriven_7), .b(undriven_8), .out(subtractor_1_out), .bin(undriven_6), .bout(subtractor_1_bout));
  Multiplier multiplier_1 (
    .a(undriven), .b(undriven_2), .out(multiplier_1_out), .cin(undriven_9), .cout(multiplier_1_cout));
  Divider divider_1 (.a(undriven_4), .b(undriven_5), .out(divider_1_out), .upper(undriven_3), .rem(divider_1_rem));
  Negator negator_1 (.in(in_27), .out(out_61));
  Comparator comparator_1 ();  // open: a, b, gt, eq, lt
  Shifter #(.shift("ar")) shifter_1 (.in(in_33), .\dist (in_34), .out(out_63));
  BitFinder bitfinder_1 (.in(in_42), .index(out_67));  // open: found
  Comparator #(.mode("unsigned")) comparator_2 ();  // open: a, b, gt, eq, lt
  BitAdder bitadder_1 (.in0(in_39), .out(out_65));
  Priority_Encoder priority_encoder_2 (
    .in0(in_42[0]), .in1(in_42[1]), .in2(in_42[2]), .in3(in_42[3]), .in4(in_42[4]), .in5(in_42[5]),
    .in6(in_42[6]), .in7(in_42[7]), .out(\找最高的1 ));  // open: en_in, gs, en_out
  Priority_Encoder priority_encoder_3 (
    .in0(in_42[7]), .in1(in_42[6]), .in2(in_42[5]), .in3(in_42[4]), .in4(in_42[3]), .in5(in_42[2]),
    .in6(in_42[1]), .in7(in_42[0]), .out(out_69));  // open: en_in, gs, en_out
  D_Flip_Flop d_ff_1 ();  // open: clk, D, Q, Qn, preset, en, reset
  T_Flip_Flop t_ff_1 ();  // open: clk, T, Q, Qn, preset, reset, en
  J_K_Flip_Flop j_k_ff_1 ();  // open: J, clk, K, Q, Qn, preset, en, reset
  S_R_Flip_Flop s_r_ff_1 ();  // open: S, clk, R, Q, Qn, preset, reset, en
  Register register_1 ();  // open: D, en, Q, clk, clr
  Counter counter_1 ();  // open: load, D, count, Q, carry, clk, clr
  Random random_1 ();  // open: clk, next, out, clr
  Clock clock_2 (.out(clock_2_out));
  ROM rom_1 ();  // open: addr, data, sel
  RAM #(.bus("separate")) ram_1 ();  // open: addr, din, data, str, sel, clk, ld, clr
  Shift_Register shift_register_1 (
    .shift(\移位 ), .in(in_22), .clk(clock_2_out), .out(out_50), .load(\加载 ), .clr(reset), .d0(in_7),
    .q0(out_53), .d1(in_8), .q1(out_54), .d2(in_9), .q2(out_55), .d3(in_10), .q3(out_56), .d4(in_12),
    .q4(out_57), .d5(in_13), .q5(out_58), .d6(in_14), .q6(out_59), .d7(in_15), .q7(out_60));

  // Notes on the sheet:
  //   和上面差不多，只是组合了一个取反
  //   某一列有奇数个1在输出端对应的那一列就会为1
  //   某一列有偶数个1在输出端对应的那一列就会为1
  //   选择为1的时候起缓冲作用否则就输出浮动的值
  //   选择往哪一路里面载入值
  //   选择把第几路输出置为1
  //   是否有1
  //   载入某一位的值
  //   这边没有符号位，只是按位变反然后加了1
  //   ？
  //   可以考虑溢出
  //   还是有一点不理解 不太知道怎么用
  //   计算有多少位为1
  //   找最低的1
  //   输入
  //   加载的优先度要高于移位，在执行加载功能的时候会把北面的8位数加载过去，在执行移位功能的时候会像右移动然后左边填充输入的一位data
endmodule
